# Fritzing sketch Connector (saved by Fritzing 0.9.3b)
circuit board: 8.63954cm x 7.69003cm
breadboards: 1

parts:
  DISPLAY1 = female pin header, 6 pins [form="♀ (female)"]
  GPIO1 = female pin header, 1 pin [form="♀ (female)"]
  UART1 = female pin header, 3 pins [form="♀ (female)"]
  1-Wire1 = female pin header, 1 pin [form="♀ (female)"]
  RELAYS1 = female pin header, 5 pins [form="♀ (female)"]
  J2 = double row female pin header, 26 pins [form="♀ (female)"]
  Power1 = female pin header, 2 pins [form="♀ (female)"]

nets:
  N1: DISPLAY1.pin1, J2.pin15
  N2: DISPLAY1.pin2, J2.pin16
  N3: DISPLAY1.pin3, J2.pin14
  N4: DISPLAY1.pin4, J2.pin10
  N5: DISPLAY1.pin5, J2.pin12
  N6: DISPLAY1.pin6, J2.pin8
  N7: GPIO1.pin1, J2.pin4
  N8: UART1.pin1, J2.pin23
  N9: UART1.pin2, J2.pin22
  N10: UART1.pin3, Power1.pin2
  N11: 1-Wire1.pin1, J2.pin3
  N12: RELAYS1.pin1, J2.pin18
  N13: RELAYS1.pin2, RELAYS1.pin3, J2.pin19, J2.pin21
  N14: RELAYS1.pin4, J2.pin6
  N15: RELAYS1.pin5, J2.pin7
